# Fritzing sketch Wiring (saved by Fritzing 0.9.3b)
breadboards: 1

parts:
  PWM1 = PCA9685 16x12-bit PWM Breakout
  Part1 = Arduino Uno (Rev3) - ICSP
  S1 = Momentary Switch [package=ksa_sealed_tac_switch]
  S2 = Momentary Switch [package=ksa_sealed_tac_switch]
  S3 = Momentary Switch [package=ksa_sealed_tac_switch]
  S4 = Momentary Switch [package=ksa_sealed_tac_switch]
  S5 = Momentary Switch [package=ksa_sealed_tac_switch]
  S6 = Momentary Switch [package=ksa_sealed_tac_switch]
  Part2 = Adafruit Micro USB Breakout [part_number="Adafruit #1833"]  # not connected
  S7 = Momentary Switch [package=ksa_sealed_tac_switch]
  S8 = Momentary Switch [package=ksa_sealed_tac_switch]
  S9 = Momentary Switch [package=ksa_sealed_tac_switch]
  S10 = Momentary Switch [package=ksa_sealed_tac_switch]
  S11 = Momentary Switch [package=ksa_sealed_tac_switch]
  S12 = Momentary Switch [package=ksa_sealed_tac_switch]

nets:
  N1: PWM1.no_name_yet#601, S1.2, S2.2, S3.1, S3.2, S4.3, S4.4, S5.1, S5.2, S6.3, S6.4, S7.1, S7.2, S8.3, S8.4, S9.1, S9.4, S10.1, S10.4, S11.1, S11.2, S12.3, S12.4
  N2: PWM1.no_name_yet#603, Part1.A5/SCL
  N3: PWM1.no_name_yet#604, Part1.A4/SDA
  N4: PWM1.no_name_yet#605, Part1.GND
  N5: Part1.D8, S7.3, S7.4
  N6: Part1.D9_PWM, S8.1, S8.2
  N7: Part1.D10_PWM/SS, S9.3
  N8: Part1.D11_PWM/MOSI, S10.3
  N9: Part1.D12/MISO, S11.3, S11.4
  N10: Part1.D13/SCK, S12.1, S12.2
  N11: Part1.D2, S1.3
  N12: Part1.D3_PWM, S2.3
  N13: Part1.D4, S3.3, S3.4
  N14: Part1.D5_PWM, S4.1, S4.2
  N15: Part1.D6_PWM, S5.3, S5.4
  N16: Part1.D7, S6.1, S6.2

custom parts:
  Adafruit Micro USB Breakout: Simple but effective - this breakout board has a USB Micro-B connector, with all 5 pins broken out. Great for pairing with a microcontroller with USB support, or adding USB 5V power to a project. We use a micro-AB connector with through-hole shielding pads for an excellent strong connection - it won't rip off by accident! Comes with one fully assembled and tested micro B breakout PCB and a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
